# Fritzing sketch SimpleBuzzerSchematic (saved by Fritzing 1.0.6)
breadboards: 1

parts:
  Passive_Piezo_Buzzer = Piezo Speaker

nets:
  GPIO25 (PWM ~): Passive_Piezo_Buzzer.pin1
  GND: Passive_Piezo_Buzzer.pin2

notes:
  +
  -
