# Fritzing sketch TraditionalCapacitiveSensorSchematic (saved by Fritzing 1.0.6)
breadboards: 1

parts:
  R1 = Resistor [tolerance=±5% power=0.25W resistance=1M package=THT]

nets:
  D5 (Tx): R1.Pin_0
  D18 (Rx)/Sensor (wire or foil): R1.Pin_1
