# Fritzing sketch VibrationMotorFixedDistanceSensorHapticInteraction (saved by Fritzing 1.0.6)
breadboards: 1

parts:
  L293D_-_IC = L293D [package=THT]
  M1_(Vibration_Motor) = DC Motor [voltage_(max)=6V voltage_(min)=3V]
  HC-SR04_Sensor_1 = HC-SR04 Ultrasonic Distance Sensor
  R1 = Resistor [tolerance=±5% resistance=1k package="0603 [SMD]"]
  R2 = Resistor [tolerance=±5% resistance=2k package="0603 [SMD]"]

nets:
  GPIO 13: L293D_-_IC.Enable_1
  GPIO 12: L293D_-_IC.In_1
  N1: L293D_-_IC.Out_1_(_Controlled_by_Enable_1_), M1_(Vibration_Motor).pin_1
  GND: L293D_-_IC.0V, HC-SR04_Sensor_1.GND, R2.Pin_1
  N2: L293D_-_IC.Out_2_(_Controlled_by_Enable_1_), M1_(Vibration_Motor).pin_2
  GPIO 14: L293D_-_IC.In_2
  Vin (5V USB Power): L293D_-_IC.+Vmotor, L293D_-_IC.+V, HC-SR04_Sensor_1.VCC
  GPIO 19: HC-SR04_Sensor_1.TRIG
  N3: HC-SR04_Sensor_1.ECHO, R1.Pin_0
  GPIO 21: R1.Pin_1, R2.Pin_0

notes:
  This voltage divider below ensures the ESP32 (3.3V) doesn't receive 5V from the Echo Pin!
